# Fritzing sketch i2c_raspberry (saved by Fritzing 0.8.5b)

parts:
  Raspberry_Pi_B_rev1 = Raspberry Pi B rev2
  Componente1 = Arduino Uno (Rev3) - ICSP
  LED1 = LEDs [package=led10mm]

nets:
  N1: Raspberry_Pi_B_rev1.3V3, Raspberry_Pi_B_rev1.GPIO_2
  GND: Raspberry_Pi_B_rev1.GND, Componente1.GND, LED1.A
  5V: Raspberry_Pi_B_rev1.5V, Componente1.5V
  N2: Componente1.D13/SCK, LED1.C

// code stored in the sketch: i2c_raspberry.ino
#include <Wire.h>

#define SLAVE_ADDRESS 0x04
int number = 0;
int state = 0;

void setup() {
    pinMode(13, OUTPUT);
    Serial.begin(9600);

    Wire.begin(SLAVE_ADDRESS);
    Wire.onReceive(receiveData);
    Wire.onRequest(sendData);

    Serial.println("Ready!");
}

void loop() {
    delay(100);
}

void receiveData(int byteCount){

    while(Wire.available()) {
        number = Wire.read();
        Serial.print("data received: ");
        Serial.println(number);

        if (number == 1){

            if (state == 0){
                digitalWrite(13, HIGH);
                state = 1;
            }
            else{
                digitalWrite(13, LOW);
                state = 0;
            }
         }
     }
}

void sendData(){
    Wire.write(number);
}
