# Fritzing sketch raspberry_motor (saved by Fritzing 0.8.5b)
breadboards: 1

parts:
  Raspberry_Pi_B_rev1 = Raspberry Pi B rev2
  IC1 = H-Bridge [package=THT]
  M1 = Stepper Motor - Bipolar
  S1 = Square Pushbutton

nets:
  N1: Raspberry_Pi_B_rev1.3V3, S1.leg0
  N2: Raspberry_Pi_B_rev1.5V, IC1.1_2EN, IC1.VCC2, IC1.3_4EN
  GND: Raspberry_Pi_B_rev1.GND, IC1.GND1, IC1.GND2, IC1.GND3, IC1.GND4
  N3: Raspberry_Pi_B_rev1.GPIO_23, IC1.2A
  N4: Raspberry_Pi_B_rev1.GPIO_17, IC1.4A
  N5: Raspberry_Pi_B_rev1.GPIO_18, IC1.3A
  N6: Raspberry_Pi_B_rev1.GPIO_22, IC1.1A
  N7: Raspberry_Pi_B_rev1.GPIO_25, S1.leg1
  N8: IC1.1Y, M1.B
  N9: IC1.2Y, M1.D
  N10: IC1.3Y, M1.C
  N11: IC1.4Y, M1.A
