# Fritzing sketch spi_mcp_raspberry (saved by Fritzing 0.8.5b)
breadboards: 1

parts:
  IC1 = MCP3008 8-channel 10-bit ADC [part_number=MCP3008]
  Raspberry_Pi_B_rev1 = Raspberry Pi B rev2
  U1 = POT [package=pot_alpha_rv16af-20]

nets:
  N1: IC1.no_name_yet#1, U1.S
  N2: IC1.no_name_yet#9, IC1.no_name_yet#14, Raspberry_Pi_B_rev1.GND, U1.E
  N3: IC1.no_name_yet#10, Raspberry_Pi_B_rev1.GPIO_8
  N4: IC1.no_name_yet#11, Raspberry_Pi_B_rev1.GPIO_10
  N5: IC1.no_name_yet#12, Raspberry_Pi_B_rev1.GPIO_9
  N6: IC1.no_name_yet#13, Raspberry_Pi_B_rev1.GPIO_11
  N7: IC1.no_name_yet#15, IC1.no_name_yet#16, Raspberry_Pi_B_rev1.3V3, U1.A
